# Fritzing sketch Esquematico (saved by Fritzing 1.0.6)
breadboards: 1

parts:
  OLED_I2C1 = OLED 128x64 I2C Monochrome Display
  R1 = Photocell (LDR) [power=0.25W dark_resistance_@0.01lx=300kΩ light_resistance_@100lx=400Ω luminance=10lx package=THT]
  Mod1 = Passive Buzzer
  HC-SR04_Sensor_1 = HC-SR04 Ultrasonic Distance Sensor
  S1 = Pushbutton [package="[THT]"]
  R2 = Resistor [tolerance=±5% resistance=10k package="2512 [SMD]"]
  M1 = DOIT Esp32 DevKit v1 (30 pins long, 11 pins width) [part_number=ESP32S-PIN30]
  R3 = Resistor [tolerance=±5% resistance=10k package="2512 [SMD]"]
  R4 = Resistor [tolerance=±5% resistance=2k package="2512 [SMD]"]

nets:
  N1: OLED_I2C1.SDA, M1.D22
  N2: OLED_I2C1.SCK, M1.D21
  VDD: OLED_I2C1.VDD, M1.3V3
  GND: OLED_I2C1.GND, Mod1.-, HC-SR04_Sensor_1.GND, S1.Pin_1, S1.Pin_2, S1.Pin_3, S1.Pin_4, M1.GND, M1.D33, R4.Pin_1
  N3: R1.pin_1, R2.Pin_0, M1.D34
  N4: Mod1.NC, M1.D18
  VCC: HC-SR04_Sensor_1.VCC, M1.VIN
  N5: HC-SR04_Sensor_1.TRIG, M1.D14
  N6: HC-SR04_Sensor_1.ECHO, R3.Pin_0
  N7: M1.D27, R3.Pin_1, R4.Pin_0

custom parts:
  DOIT Esp32 DevKit v1 (30 pins long, 11 pins width): The DOIT Esp32 DevKit v1 is one of the development board created by DOIT to evaluate the ESP-WROOM-32 module. It is based on the ESP32 microcontroller that boasts Wifi, Bluetooth, Ethernet and Low Power support all in a single chip. (vanepp) made breadboard work, adjusted pin numbering and labels and reduced size of schematic and cleaned up pcb. This chip is 30pins long (2 x15) and 11 pins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
